# Fritzing sketch adaptador_tiva (saved by Fritzing 0.9.1b)
circuit board: 8.46667cm x 5.64444cm
breadboards: 1

parts:
  1 = Tiva Header 1 [form="♀ (female)" package=THT]
  2 = Tiva Header 2 [form="♀ (female)" package=THT]
  ATmega168 = atmega168 hockey [package=dip]
  3 = Tiva Header 3 [form="♀ (female)" package=THT]
  4 = Tiva Header 4 [form="♀ (female)" package=THT]

nets:
  N1: 1.+3.3V, ATmega168.3.3V_(AREF)
  N2: 1.PB5, ATmega168.MEIAPONTE1
  N3: 1.PB4, ATmega168.MEIAPONTE0
  N4: 1.PA6, ATmega168.SCL
  N5: 1.PA7, ATmega168.SDA
  GND: 2.GND, ATmega168.GND
  N6: 2.PD0_/_PB6, ATmega168.SCK
  N7: 2.PD2, ATmega168.MOSI
  N8: 2.PD3, ATmega168.MISO
  N9: 2.PE1, ATmega168.Botão
  N10: 2.PE2, ATmega168.BATT_V
  N11: ATmega168.RESET, 4.RST
  N12: ATmega168.RX, 3.PD6
  N13: ATmega168.TX, 3.PD7
  N14: ATmega168.INT0, 3.PC7
  N15: ATmega168.INT1, 3.PC6
  N16: ATmega168.MEIAPONTE2, 3.PC5
  N17: ATmega168.MEIAPONTE3, 3.PC4
  N18: ATmega168.LED_BATT, 4.PB7_/_PD1
  N19: ATmega168.LED_STATUS, 4.PB6_/_PD0

notes:
  G
  B
  R
  SW1
  RST
  GND
  5V
  3.3V
  SW2
  U2Rx
  I2C1SCL
  I2C1SDA
  AIN1
  SSI3Rx
  SSI3Tx
  SSI3Clk
  M0PWM3
  M0PWM1
  M0PWM0
  M0PWM2
  M0PWM6
  M0PWM7
  PC7_INT
  PC6_INT
  PE1_INT
  U2Tx

custom parts:
  Tiva Header 1: Tiva C Series Launchpad Header 1
  Tiva Header 2: Tiva C Series Launchpad Header 2
  atmega168 hockey: Atmel ATmega168 do hockey.
  Tiva Header 3: Tiva C Series Launchpad Header 3
  Tiva Header 4: Tiva C Series Launchpad Header 4
